# Fritzing sketch Tank Sensor (saved by Fritzing 0.9.4)
circuit board: 6.48284cm x 5.94381cm

parts:
  WeMos_D1_Mini1 = WeMos D1 Mini
  90% = LED - 5mm [color="Green (555nm)" package="5 mm [THT]"]
  70% = LED - 5mm [color="Green (555nm)" package="5 mm [THT]"]
  10% = LED - 5mm [color="Red (633nm)" package="5 mm [THT]"]
  20% = LED - 5mm [color="Red (633nm)" package="5 mm [THT]"]
  40% = LED - 5mm [color="Yellow (595nm)" package="5 mm [THT]"]
  50% = LED - 5mm [color="Yellow (592nm)" package="5 mm [THT]"]
  R4 = Resistor [tolerance=±5% resistance=220 package=THT]
  R3 = Resistor [tolerance=±5% resistance=220 package=THT]
  R2 = Resistor [tolerance=±5% resistance=220 package=THT]
  R1 = Resistor [tolerance=±5% resistance=220 package=THT]
  R5 = Resistor [tolerance=±5% resistance=220 package=THT]
  R6 = Resistor [tolerance=±5% resistance=220 package=THT]
  R7 = Resistor [tolerance=±5% resistance=220 package=THT]
  30% = LED - 5mm [color="Red (633nm)" package="5 mm [THT]"]
  HC-SR04 = HC-SR04 Ultrasonic Distance Sensor

nets:
  5V: WeMos_D1_Mini1.5V, HC-SR04.VCC
  N1: WeMos_D1_Mini1.D0, R5.Pin_0
  N2: WeMos_D1_Mini1.D1, R6.Pin_0
  N3: WeMos_D1_Mini1.D2, R7.Pin_0
  N4: WeMos_D1_Mini1.D3, HC-SR04.ECHO
  N5: WeMos_D1_Mini1.D4, HC-SR04.TRIG
  N6: WeMos_D1_Mini1.D5, R4.Pin_0
  N7: WeMos_D1_Mini1.D6, R3.Pin_0
  N8: WeMos_D1_Mini1.D7, R2.Pin_0
  N9: WeMos_D1_Mini1.D8, R1.Pin_0
  N10: WeMos_D1_Mini1.G, 90%.cathode, 70%.cathode, 10%.cathode, 20%.cathode, 40%.cathode, 50%.cathode, 30%.cathode, HC-SR04.GND
  N11: 90%.anode, R1.Pin_1
  N12: 70%.anode, R2.Pin_1
  N13: 10%.anode, R7.Pin_1
  N14: 20%.anode, R6.Pin_1
  N15: 40%.anode, R4.Pin_1
  N16: 50%.anode, R3.Pin_1
  N17: R5.Pin_1, 30%.anode

notes:
  Tank level sensor
  By RedFoxy Darrest
  https://me.redfoxy.it
